# Fritzing sketch Assistente vocale con modulo Bluetooth HC-05 e Arduino UNO (saved by Fritzing 0.9.6b)
breadboards: 1

parts:
  Componente1 = Bluetooth HC-05 Macho
  Componente2 = Arduino Uno (Rev3)
  R1 = Resistor [tolerance=±5% power=0.25 resistance=2.2k package=THT]
  R2 = Resistor [tolerance=±5% power=0.25W resistance=1k package=THT]
  LED1 = LED - 5mm [color="Red (633nm)" current=0.030 package="5 mm [THT]"]  # not connected
  R3 = Resistor [tolerance=±5% power=0.25 resistance=220 package=THT]

nets:
  N1: Componente1.TXD, Componente2.D10_PWM/SS
  N2: Componente1.RXD, R2.Pin_0
  VCC: Componente1.VCC, Componente2.5V
  GND: Componente1.GND, Componente2.GND, R1.Pin_0
  N3: Componente2.D11_PWM/MOSI, R1.Pin_1, R2.Pin_1
  N4: Componente2.D3_PWM, R3.Pin_0
